// Digital circuit CONTROL.dig as structural Verilog
module CONTROL (
  input  Control,
  input  In,
  output Out
);

  wire [63:0] bussplitter_1_d;

  BusSplitter #(.Bits(64), .generic("this.Bits = args.bitWidth;")) bussplitter_1 (
    .D(bussplitter_1_d), .OE(1'b0), .D0(Control), .D1(Control), .D2(Control), .D3(Control), .D4(Control),
    .D5(Control), .D6(Control), .D7(Control), .D8(Control), .D9(Control), .D10(Control), .D11(Control),
    .D12(Control), .D13(Control), .D14(Control), .D15(Control), .D16(Control), .D17(Control), .D18(Control),
    .D19(Control), .D20(Control), .D21(Control), .D22(Control), .D23(Control), .D24(Control), .D25(Control),
    .D26(Control), .D27(Control), .D28(Control), .D29(Control), .D30(Control), .D31(Control), .D32(Control),
    .D33(Control), .D34(Control), .D35(Control), .D36(Control), .D37(Control), .D38(Control), .D39(Control),
    .D40(Control), .D41(Control), .D42(Control), .D43(Control), .D44(Control), .D45(Control), .D46(Control),
    .D47(Control), .D48(Control), .D49(Control), .D50(Control), .D51(Control), .D52(Control), .D53(Control),
    .D54(Control), .D55(Control), .D56(Control), .D57(Control), .D58(Control), .D59(Control), .D60(Control),
    .D61(Control), .D62(Control), .D63(Control));
  assign Out = {64{In}} & bussplitter_1_d;  // And and_1, 64 bits wide
endmodule
