// Digital circuit clock.dig as structural Verilog
module clock (
  input  C,
  output _1,
  output _1_1,
  output _2
);

  wire and_1_out, flipflop_1_value, flipflop_2_value, flipflop_3_value, flipflop_4_value, flipflop_5_value,
       flipflop_6_value, not_1_out, not_2_out, or_1_out, or_2_out, or_3_out, or_4_out, or_5_out;

  or or_1 (or_1_out, or_1_out, C);
  not not_1 (not_1_out, C);
  not not_2 (not_2_out, or_1_out);
  or or_2 (or_2_out, not_2_out, flipflop_6_value);
  and and_1 (and_1_out, or_2_out, ~flipflop_2_value);  // And
  flipflop flipflop_1 (.Data(and_1_out), .Write(not_1_out), .Value(flipflop_1_value));
  flipflop flipflop_2 (.Data(flipflop_1_value), .Write(C), .Value(flipflop_2_value));
  flipflop flipflop_3 (.Data(flipflop_2_value), .Write(not_1_out), .Value(flipflop_3_value));
  flipflop flipflop_4 (.Data(flipflop_3_value), .Write(C), .Value(flipflop_4_value));
  flipflop flipflop_5 (.Data(flipflop_4_value), .Write(not_1_out), .Value(flipflop_5_value));
  flipflop flipflop_6 (.Data(flipflop_5_value), .Write(C), .Value(flipflop_6_value));
  or or_3 (or_3_out, flipflop_1_value, flipflop_3_value);
  and and_2 (_1, or_3_out, ~flipflop_2_value);  // And
  or or_4 (or_4_out, flipflop_2_value, flipflop_4_value);
  or or_5 (or_5_out, flipflop_3_value, flipflop_5_value);
  and and_3 (_1_1, or_4_out, ~flipflop_3_value);  // And
  and and_4 (_2, or_5_out, ~flipflop_4_value);  // And

  // Notes on the sheet:
  //   I am sure this is horribly inefficient,
  //   but it works!
endmodule
