// Digital circuit current_symbol.dig as structural Verilog
module current_symbol (
  input  Write,
  input  [3:0] Data,
  output [15:0] Value
);

  wire [3:0] tapecell_1_value;

  Decoder #(.Selector_Bits(4)) decoder_1 (
    .sel(tapecell_1_value), .out_0(Value[0]), .out_1(Value[1]), .out_2(Value[2]), .out_3(Value[3]),
    .out_4(Value[4]), .out_5(Value[5]), .out_6(Value[6]), .out_7(Value[7]), .out_8(Value[8]),
    .out_9(Value[9]), .out_10(Value[10]), .out_11(Value[11]), .out_12(Value[12]), .out_13(Value[13]),
    .out_14(Value[14]), .out_15(Value[15]));
  tapecell tapecell_1 (.Data(Data), .Write(Write), .Value(tapecell_1_value));
endmodule
