// Digital circuit flipflop.dig as structural Verilog
module flipflop (
  input  Data,
  input  Write,
  output Value
);

  wire and_1_out, and_2_out, not_1_out, not_2_out, or_1_out;

  not not_1 (not_1_out, Data);
  and and_1 (and_1_out, Data, Write);
  and and_2 (and_2_out, Write, not_1_out);
  or or_1 (or_1_out, Value, and_1_out);
  not not_2 (not_2_out, and_2_out);
  and and_3 (Value, or_1_out, not_2_out);

  // Notes on the sheet:
  //   Value: The value curently stored
  //   Data: The value written when `Write` is high
  //   Write: Writes `Data` when high
endmodule
