// Digital circuit init.dig as structural Verilog
module init (
  input  Action,
  input  [15:0] Lookup,
  output SHL,
  output SHR,
  output left,
  output _0,
  output _1,
  output out_6,
  output done
);

  wire initstate_1_q, initstate_2_q, initstate_3_q, initstate_4_q, predone, start_1_acto, start_1_fqo,
       state_1_p5;

  // state #(.generic("shift := 0x8000;")) state_1: pin names not known; wires that end beside it: predone, Action, Lookup, left, state_1_p5, _0, predone, _1, predone, out_6, predone
  // state #(.generic("shift := 0xFFFF;")) state_2: pin names not known; wires that end beside it: state_1_p5, Action, Lookup, _0, done, _1, done, out_6, done
  start start_1 (.fqi(1'b0), .Acti(Action), .fqo(start_1_fqo), .Acto(start_1_acto));
  initstate initstate_1 (.Action(start_1_acto), .Q(initstate_1_q), .Shift(SHR), .\Γ (left), .from_q(start_1_fqo));
  initstate initstate_2 (.Action(Action), .Q(initstate_2_q), .Shift(SHR), .\Γ (_0), .from_q(initstate_1_q));
  initstate initstate_3 (.Action(Action), .Q(initstate_3_q), .Shift(SHR), .\Γ (_1), .from_q(initstate_2_q));
  initstate initstate_4 (.Action(Action), .Q(initstate_4_q), .Shift(SHR), .\Γ (out_6), .from_q(initstate_3_q));
  initstate initstate_5 (.Action(Action), .Q(predone), .Shift(SHL), .\Γ (_0), .from_q(initstate_4_q));

  // Other names for the same wires on the sheet: tunnel = out_6
endmodule
