// Digital circuit inithigh.dig as structural Verilog
// Emits 1 on startup, but as soon as the clock is high, switches to 0 permanently.  
// Useful for setting values on startup.
module inithigh (
  input  C,
  output O
);

  wire or_1_out;

  or or_1 (or_1_out, or_1_out, C);
  not not_1 (O, or_1_out);
endmodule
