// Digital circuit initstate.dig as structural Verilog
module initstate (
  input  Action,
  input  from_q,
  output Q,
  output \Γ ,
  output Shift
);

  // state #(.generic("shift := 0;")) state_1: pin names not known; wires that end beside it: from_q, Action, {16{1'b0}}, \Γ , Q, \Γ , Q, \Γ , Q, \Γ , Q, \Γ , Q, \Γ , Q, \Γ , Q, \Γ , Q, \Γ , Q, \Γ , Q, \Γ , Q, \Γ , Q, \Γ 

  // Other names for the same wires on the sheet: g = \Γ 
endmodule
