// Digital circuit main.dig as structural Verilog
module main (
  input  clk
);

  wire and_1_out, and_2_out, and_3_out, and_4_out, clock_1__1, clock_1__1_1, clock_1__2, init_1_done,
       init_1_shl, init_1_shr, or_2_out, or_3_out, statemachine_1_out_7, statemachine_1_out_8,
       statemachine_1_shl, statemachine_1_shr, \statemachine_1_γ , tapechunk1000_1_lout,
       tapechunk1000_1_rout, tapechunk1000_2_lout, tapechunk1000_2_rout, tapechunk1000_3_lout,
       tapechunk1000_3_rout, tapechunk1000_4_lout, tapechunk1000_4_rout, tapechunk1000_5_lout,
       tapechunk1000_5_rout, tapechunk1000_6_lout, tapechunk1000_6_rout, tapechunk1000_7_lout,
       tapechunk1000_7_rout, tapechunk1000_8_lout, tapechunk1000_8_rout, tapechunk1000_9_lout,
       tapechunk1000_9_rout, tapechunk1000_10_lout, tapechunk1000_10_rout;
  wire [3:0] init_1_left, priorityencoder_1_num, tapechunk1000_1_value;
  wire [15:0] current_symbol_1_value, or_1_out;

  clock clock_1 (.C(clk), ._1(clock_1__1), ._1_1(clock_1__1_1), ._2(clock_1__2));
  current_symbol current_symbol_1 (.Write(clock_1__1), .Data(tapechunk1000_1_value), .Value(current_symbol_1_value));
  statemachine statemachine_1 (
    .Start(init_1_done), .Activating(clock_1__2), .Lookup(current_symbol_1_value), .SHL(statemachine_1_shl),
    .SHR(statemachine_1_shr), .\Γ (\statemachine_1_γ ), .out_7(statemachine_1_out_7),
    .out_8(statemachine_1_out_8));
  init init_1 (
    .SHL(init_1_shl), .SHR(init_1_shr), .left(init_1_left[3]), ._0(init_1_left[2]), ._1(init_1_left[1]),
    .out_6(init_1_left[0]), .done(init_1_done), .Action(clock_1__2), .Lookup(current_symbol_1_value));
  LED led_1 (.in(statemachine_1_out_7));
  Stop stop_1 (.stop(statemachine_1_out_7));
  LED led_2 (.in(statemachine_1_out_8));
  Stop stop_2 (.stop(statemachine_1_out_8));
  or or_1 (or_1_out[0], 1'b0, \statemachine_1_γ );
  PriorityEncoder #(.Selector_Bits(4)) priorityencoder_1 (
    .in0(or_1_out[0]), .in1(or_1_out[1]), .in2(or_1_out[2]), .in3(or_1_out[3]), .in4(or_1_out[4]),
    .in5(or_1_out[5]), .in6(or_1_out[6]), .in7(or_1_out[7]), .in8(or_1_out[8]), .in9(or_1_out[9]),
    .in10(or_1_out[10]), .in11(or_1_out[11]), .in12(or_1_out[12]), .in13(or_1_out[13]), .in14(or_1_out[14]),
    .in15(or_1_out[15]), .num(priorityencoder_1_num));  // open: any
  or or_2 (or_2_out, init_1_shl, statemachine_1_shl);
  and and_1 (and_1_out, or_3_out, clock_1__1_1);
  and and_2 (and_2_out, or_2_out, clock_1__1_1);
  tapechunk1000 tapechunk1000_1 (
    .Lin(1'b0), .Rout(tapechunk1000_1_rout), .Write(clock_1__1_1), .Data(priorityencoder_1_num),
    .SHL(and_2_out), .SHR(and_1_out), .Value(tapechunk1000_1_value), .Lout(tapechunk1000_1_lout),
    .Rin(tapechunk1000_2_rout));
  tapechunk1000 tapechunk1000_2 (
    .Lin(tapechunk1000_1_lout), .Rout(tapechunk1000_2_rout), .Write(clock_1__1_1),
    .Data(priorityencoder_1_num), .SHL(and_2_out), .SHR(and_1_out), .Value(tapechunk1000_1_value),
    .Lout(tapechunk1000_2_lout), .Rin(tapechunk1000_3_rout));
  tapechunk1000 tapechunk1000_3 (
    .Lin(tapechunk1000_2_lout), .Rout(tapechunk1000_3_rout), .Write(clock_1__1_1),
    .Data(priorityencoder_1_num), .SHL(and_2_out), .SHR(and_1_out), .Value(tapechunk1000_1_value),
    .Lout(tapechunk1000_3_lout), .Rin(tapechunk1000_4_rout));
  tapechunk1000 tapechunk1000_4 (
    .Lin(tapechunk1000_3_lout), .Rout(tapechunk1000_4_rout), .Write(clock_1__1_1),
    .Data(priorityencoder_1_num), .SHL(and_2_out), .SHR(and_1_out), .Value(tapechunk1000_1_value),
    .Lout(tapechunk1000_4_lout), .Rin(tapechunk1000_5_rout));
  tapechunk1000 tapechunk1000_5 (
    .Lin(tapechunk1000_4_lout), .Rout(tapechunk1000_5_rout), .Write(clock_1__1_1),
    .Data(priorityencoder_1_num), .SHL(and_2_out), .SHR(and_1_out), .Value(tapechunk1000_1_value),
    .Lout(tapechunk1000_5_lout), .Rin(tapechunk1000_6_rout));
  tapechunk1000 tapechunk1000_6 (
    .Lin(tapechunk1000_5_lout), .Rout(tapechunk1000_6_rout), .Write(clock_1__1_1),
    .Data(priorityencoder_1_num), .SHL(and_2_out), .SHR(and_1_out), .Value(tapechunk1000_1_value),
    .Lout(tapechunk1000_6_lout), .Rin(tapechunk1000_7_rout));
  tapechunk1000 tapechunk1000_7 (
    .Lin(tapechunk1000_6_lout), .Rout(tapechunk1000_7_rout), .Write(clock_1__1_1),
    .Data(priorityencoder_1_num), .SHL(and_2_out), .SHR(and_1_out), .Value(tapechunk1000_1_value),
    .Lout(tapechunk1000_7_lout), .Rin(tapechunk1000_8_rout));
  tapechunk1000 tapechunk1000_8 (
    .Lin(tapechunk1000_7_lout), .Rout(tapechunk1000_8_rout), .Write(clock_1__1_1),
    .Data(priorityencoder_1_num), .SHL(and_2_out), .SHR(and_1_out), .Value(tapechunk1000_1_value),
    .Lout(tapechunk1000_8_lout), .Rin(tapechunk1000_9_rout));
  tapechunk1000 tapechunk1000_9 (
    .Lin(tapechunk1000_8_lout), .Rout(tapechunk1000_9_rout), .Write(clock_1__1_1),
    .Data(priorityencoder_1_num), .SHL(and_2_out), .SHR(and_1_out), .Value(tapechunk1000_1_value),
    .Lout(tapechunk1000_9_lout), .Rin(tapechunk1000_10_rout));
  tapechunk1000 tapechunk1000_10 (
    .Lin(tapechunk1000_9_lout), .Rout(tapechunk1000_10_rout), .Write(clock_1__1_1),
    .Data(priorityencoder_1_num), .SHL(and_2_out), .SHR(and_1_out), .Value(tapechunk1000_1_value),
    .Lout(tapechunk1000_10_lout), .Rin(1'b0));
  or or_3 (or_3_out, init_1_shr, statemachine_1_shr);
  Stop stop_3 (.stop(and_3_out));
  and and_3 (and_3_out, and_2_out, tapechunk1000_1_rout);
  LED led_3 (.in(tapechunk1000_10_lout));
  and and_4 (and_4_out, tapechunk1000_10_lout, and_1_out);
  LED led_4 (.in(and_4_out));
  Stop stop_4 (.stop(and_4_out));
  LED led_5 (.in(and_3_out));
  LED led_6 (.in(tapechunk1000_1_rout));
  // Pins of 1 and 16 bits meet at {init_1_left, {12{1'b0}}}
  // Pins of 1 and 16 bits meet at or_1_out

  // Notes on the sheet:
  //   Phase 1: not Activating
  //   Read from tape and write to current symbol
  //   Send out all info from state
  //   Update Am q'
  //   Phase 1.1: writing
  //   Update next tapesym
  //   Write to tape
  //   Phase 2: Activating
  //   Stop writing to Am q'
  //   Stop sending any info
  //   Update Active state
  //   Update Active tapecell
endmodule
