// Digital circuit splitdiode.dig as structural Verilog
module splitdiode (
  input  I,
  output O0,
  output O1
);

  DiodeForward diodeforward_1 (.in(I), .out(O0));
  PullDown pulldown_1 (.out(O0));
  DiodeForward diodeforward_2 (.in(I), .out(O1));
  PullDown pulldown_2 (.out(O1));
endmodule
