// Digital circuit start.dig as structural Verilog
module start (
  input  fqi,
  input  Acti,
  output fqo,
  output Acto
);

  wire not_1_out, or_1_out;

  or or_1 (or_1_out, Acti, or_1_out);
  not not_1 (not_1_out, or_1_out);
  or or_2 (fqo, fqi, not_1_out);

  assign Acto = Acti;
endmodule
