// Digital circuit state.dig as structural Verilog
module state (
  input  [15:0] Lookup,
  input  from_q,
  input  Activating,
  output Q,
  output _1_Q,
  output _0_Q,
  output _1_Q_2,
  output _0_Q_2,
  output H_Q,
  output H1_Q,
  output H0_Q,
  output Q_2,
  output _0_Q_3,
  output _1_Q_3,
  output _00_Q,
  output _01_Q,
  output _10_Q,
  output _11_Q,
  output Q_3,
  output SHL,
  output SHR,
  output \Γ ,
  output \_1_Γ ,
  output \_0_Γ ,
  output \_1_Γ_2 ,
  output \_0_Γ_2 ,
  output \H_Γ ,
  output \H1_Γ ,
  output \H0_Γ ,
  output \Γ_2 ,
  output \_0_Γ_3 ,
  output \_1_Γ_3 ,
  output \_00_Γ ,
  output \_01_Γ ,
  output \_10_Γ ,
  output \_11_Γ ,
  output \Γ_3 
);

  wire Active_value, Am_q_value, and_2_out, not_1_out, not_2_out, or_1_out;
  wire [15:0] and_1_out, control_3_out;

  splitdiode splitdiode_1 (.I(control_3_out[15]), .O0(Q), .O1(\Γ ));
  splitdiode splitdiode_2 (.I(control_3_out[14]), .O0(_0_Q), .O1(\_0_Γ ));
  splitdiode splitdiode_3 (.I(control_3_out[13]), .O0(_1_Q), .O1(\_1_Γ ));
  splitdiode splitdiode_4 (.I(control_3_out[12]), .O0(Q_3), .O1(\Γ_3 ));
  splitdiode splitdiode_5 (.I(control_3_out[11]), .O0(_00_Q), .O1(\_00_Γ ));
  splitdiode splitdiode_6 (.I(control_3_out[10]), .O0(_01_Q), .O1(\_01_Γ ));
  not not_1 (not_1_out, Activating);
  splitdiode splitdiode_7 (.I(control_3_out[9]), .O0(_10_Q), .O1(\_10_Γ ));
  flipflop Am_q (.Data(from_q), .Write(not_1_out), .Value(Am_q_value));
  splitdiode splitdiode_8 (.I(control_3_out[8]), .O0(_11_Q), .O1(\_11_Γ ));
  splitdiode splitdiode_9 (.I(control_3_out[7]), .O0(Q_2), .O1(\Γ_2 ));
  flipflop Active (.Data(Am_q_value), .Write(Activating), .Value(Active_value));
  assign and_1_out = 16'h1 & Lookup;  // And and_1, 16 bits wide
  splitdiode splitdiode_10 (.I(control_3_out[6]), .O0(_0_Q_3), .O1(\_0_Γ_3 ));
  and and_2 (and_2_out, Active_value, ~Activating);  // And
  OR or_1 (.In(and_1_out), .Out(or_1_out));
  splitdiode splitdiode_11 (.I(control_3_out[5]), .O0(_1_Q_3), .O1(\_1_Γ_3 ));
  splitdiode splitdiode_12 (.I(control_3_out[4]), .O0(_0_Q_2), .O1(\_0_Γ_2 ));
  splitdiode splitdiode_13 (.I(control_3_out[3]), .O0(_1_Q_2), .O1(\_1_Γ_2 ));
  CONTROL #(.generic("bitWidth := 1;")) control_1 (.Control(and_2_out), .In(or_1_out), .Out(SHL));
  CONTROL #(.generic("bitWidth := 1;")) control_2 (.Control(and_2_out), .In(not_2_out), .Out(SHR));
  not not_2 (not_2_out, or_1_out);
  CONTROL #(.generic("bitWidth := 16;")) control_3 (.Control(and_2_out), .In(Lookup), .Out(control_3_out));
  splitdiode splitdiode_14 (.I(control_3_out[2]), .O0(H_Q), .O1(\H_Γ ));
  splitdiode splitdiode_15 (.I(control_3_out[1]), .O0(H0_Q), .O1(\H0_Γ ));
  splitdiode splitdiode_16 (.I(control_3_out[0]), .O0(H1_Q), .O1(\H1_Γ ));

  // Notes on the sheet:
  //   Lookup: 16 bits, each corresponding to one tape symbol
  //   from_q: 1 if the current q is indicating that this is q'
  //   Activating: 1 when activated should be updated
  //   Phase 1: not Activating
  //   Send out all info
  //   Update Am q'
  //   Phase 2: Activating
  //   Stop writing to Am q'
  //   Stop sending any info
  //   Update Active
endmodule

/* Code that sets the parameters or builds the circuit:
shift := 0x3000;
*/
