// Digital circuit statemachine.dig as structural Verilog
module statemachine (
  input  Start,
  input  Activating,
  input  [15:0] Lookup,
  output SHL,
  output SHR,
  output [15:0] \Γ ,
  output out_7,
  output out_8
);

  wire name, Name_p4, Name_p5, Name_p6, Name_p7, Name_p8, Name_p9, Name_p10, Name_p11, Name_p12, Name_p13,
       Name_p14, Name_p15, Name_p16, Name_p17, Name_p18, Name_p19, Name_p20, Name_p21, Name_p22, Name_p23,
       Name_p24, Name_p25, Name_p26, Name_p27, Name_p28;

  // state #(.generic("shift := ;")) Name: pin names not known; wires that end beside it: name, Activating, Lookup, Name_p4, Name_p5, Name_p6, Name_p7, Name_p8, Name_p9, Name_p10, Name_p11, Name_p12, Name_p13, Name_p14, Name_p15, Name_p16, Name_p17, Name_p18, Name_p19, Name_p20, Name_p21, Name_p22, Name_p23, Name_p24, Name_p25, Name_p26, Name_p27, Name_p28
  // Pins of 1 and 16 bits meet at \Γ 

  // Other names for the same wires on the sheet: _0 = \Γ [6]; _00 = \Γ [11]; _0_t = \Γ [14]; _0_t_t = \Γ [4];
  //   _01 = \Γ [10]; _1 = \Γ [5]; _1_t = \Γ [13]; _1_t_t = \Γ [3]; _10 = \Γ [9]; _11 = \Γ [8]; accept = out_7;
  //   act = Activating; H = \Γ [2]; H0 = \Γ [1]; H1 = \Γ [0]; look[15:0] = Lookup; reject = out_8; tunnel = \Γ [12];
  //   tunnel_t = \Γ [7]; tunnel_t_t = \Γ [15]
endmodule
