// Digital circuit tape.dig as structural Verilog
module tape (
  input  Lin,
  input  Write,
  input  [3:0] Data,
  input  SHL,
  input  SHR,
  input  Lin_2,
  output Rout,
  output [3:0] Value,
  output Lout
);

  wire tapeseg_1_lout, tapeseg_2_lout, tapeseg_2_rout, tapeseg_3_lout, tapeseg_3_rout, tapeseg_4_lout,
       tapeseg_4_rout, tapeseg_5_lout, tapeseg_5_rout, tapeseg_6_lout, tapeseg_6_rout, tapeseg_7_lout,
       tapeseg_7_rout, tapeseg_8_lout, tapeseg_8_rout, tapeseg_9_lout, tapeseg_9_rout, tapeseg_10_rout;
  wire [3:0] or_1_out, or_2_out, or_3_out, or_4_out, or_5_out, or_6_out, or_7_out, or_8_out, tapeseg_1_value,
       tapeseg_2_value, tapeseg_3_value, tapeseg_4_value, tapeseg_5_value, tapeseg_6_value, tapeseg_7_value,
       tapeseg_8_value, tapeseg_9_value, tapeseg_10_value;

  tapeseg tapeseg_1 (
    .Write(Write), .Value(tapeseg_1_value), .SHR(SHR), .SHL(SHL), .Data(Data), .Lin(Lin), .Rout(Rout),
    .Lout(tapeseg_1_lout), .Rin(tapeseg_2_rout));
  tapeseg tapeseg_2 (
    .Write(Write), .Value(tapeseg_2_value), .SHR(SHR), .SHL(SHL), .Data(Data), .Lin(tapeseg_1_lout),
    .Rout(tapeseg_2_rout), .Lout(tapeseg_2_lout), .Rin(tapeseg_3_rout));
  tapeseg tapeseg_3 (
    .Write(Write), .Value(tapeseg_3_value), .SHR(SHR), .SHL(SHL), .Data(Data), .Lin(tapeseg_2_lout),
    .Rout(tapeseg_3_rout), .Lout(tapeseg_3_lout), .Rin(tapeseg_4_rout));
  tapeseg tapeseg_4 (
    .Write(Write), .Value(tapeseg_4_value), .SHR(SHR), .SHL(SHL), .Data(Data), .Lin(tapeseg_3_lout),
    .Rout(tapeseg_4_rout), .Lout(tapeseg_4_lout), .Rin(tapeseg_5_rout));
  tapeseg tapeseg_5 (
    .Write(Write), .Value(tapeseg_5_value), .SHR(SHR), .SHL(SHL), .Data(Data), .Lin(tapeseg_4_lout),
    .Rout(tapeseg_5_rout), .Lout(tapeseg_5_lout), .Rin(tapeseg_6_rout));
  tapeseg tapeseg_6 (
    .Write(Write), .Value(tapeseg_6_value), .SHR(SHR), .SHL(SHL), .Data(Data), .Lin(tapeseg_5_lout),
    .Rout(tapeseg_6_rout), .Lout(tapeseg_6_lout), .Rin(tapeseg_7_rout));
  tapeseg tapeseg_7 (
    .Write(Write), .Value(tapeseg_7_value), .SHR(SHR), .SHL(SHL), .Data(Data), .Lin(tapeseg_6_lout),
    .Rout(tapeseg_7_rout), .Lout(tapeseg_7_lout), .Rin(tapeseg_8_rout));
  tapeseg tapeseg_8 (
    .Write(Write), .Value(tapeseg_8_value), .SHR(SHR), .SHL(SHL), .Data(Data), .Lin(tapeseg_7_lout),
    .Rout(tapeseg_8_rout), .Lout(tapeseg_8_lout), .Rin(tapeseg_9_rout));
  tapeseg tapeseg_9 (
    .Write(Write), .Value(tapeseg_9_value), .SHR(SHR), .SHL(SHL), .Data(Data), .Lin(tapeseg_8_lout),
    .Rout(tapeseg_9_rout), .Lout(tapeseg_9_lout), .Rin(tapeseg_10_rout));
  tapeseg tapeseg_10 (
    .Write(Write), .Value(tapeseg_10_value), .SHR(SHR), .SHL(SHL), .Data(Data), .Lin(tapeseg_9_lout),
    .Rout(tapeseg_10_rout), .Lout(Lout), .Rin(Lin_2));
  assign or_1_out = tapeseg_1_value | tapeseg_2_value;  // Or or_1, 4 bits wide
  assign or_2_out = or_1_out | tapeseg_3_value;  // Or or_2, 4 bits wide
  assign or_3_out = or_2_out | tapeseg_4_value;  // Or or_3, 4 bits wide
  assign or_4_out = or_3_out | tapeseg_5_value;  // Or or_4, 4 bits wide
  assign or_5_out = or_4_out | tapeseg_6_value;  // Or or_5, 4 bits wide
  assign or_6_out = or_5_out | tapeseg_7_value;  // Or or_6, 4 bits wide
  assign or_7_out = or_6_out | tapeseg_8_value;  // Or or_7, 4 bits wide
  assign or_8_out = or_7_out | tapeseg_9_value;  // Or or_8, 4 bits wide
  assign Value = or_8_out | tapeseg_10_value;  // Or or_9, 4 bits wide
endmodule
