// Digital circuit tapecell.dig as structural Verilog
module tapecell (
  input  [3:0] Data,
  input  Write,
  output [3:0] Value
);

  wire or_1_out;
  wire [3:0] and_1_out, or_2_out;
  wire [3:3] inithigh_1_o;

  inithigh inithigh_1 (.C(Write), .O(inithigh_1_o[3]));
  assign and_1_out = 4'b0111 & {4{inithigh_1_o[3]}};  // And and_1, 4 bits wide
  or or_1 (or_1_out, inithigh_1_o[3], Write);
  assign or_2_out = Data | and_1_out;  // Or or_2, 4 bits wide
  flipflop flipflop_1 (.Data(or_2_out[0]), .Write(or_1_out), .Value(Value[0]));
  flipflop flipflop_2 (.Data(or_2_out[1]), .Write(or_1_out), .Value(Value[1]));
  flipflop flipflop_3 (.Data(or_2_out[2]), .Write(or_1_out), .Value(Value[2]));
  flipflop flipflop_4 (.Data(or_2_out[3]), .Write(or_1_out), .Value(Value[3]));
endmodule
