// Digital circuit tapechunk100.dig as structural Verilog
module tapechunk100 (
  input  Lin,
  input  Write,
  input  [3:0] Data,
  input  SHL,
  input  SHR,
  input  Rin,
  output Rout,
  output [3:0] Value,
  output Lout
);

  wire [3:0] or_1_out, or_2_out, or_3_out, or_4_out, or_5_out, or_6_out, or_7_out, or_8_out,
       tapechunk10_1_p7, tapechunk10_2_p5, tapechunk10_3_p5, tapechunk10_4_p5, tapechunk10_5_p5,
       tapechunk10_6_p5, tapechunk10_7_p5, tapechunk10_8_p5, tapechunk10_9_p5, tapechunk10_10_p7;

  // tapechunk10 tapechunk10_1: pin names not known; wires that end beside it: Write, Data, SHL, SHR, Lin, Rout, tapechunk10_1_p7
  // tapechunk10 tapechunk10_2: pin names not known; wires that end beside it: Write, Data, SHL, SHR, tapechunk10_2_p5
  // tapechunk10 tapechunk10_3: pin names not known; wires that end beside it: Write, Data, SHL, SHR, tapechunk10_3_p5
  // tapechunk10 tapechunk10_4: pin names not known; wires that end beside it: Write, Data, SHL, SHR, tapechunk10_4_p5
  // tapechunk10 tapechunk10_5: pin names not known; wires that end beside it: Write, Data, SHL, SHR, tapechunk10_5_p5
  // tapechunk10 tapechunk10_6: pin names not known; wires that end beside it: Write, Data, SHL, SHR, tapechunk10_6_p5
  // tapechunk10 tapechunk10_7: pin names not known; wires that end beside it: Write, Data, SHL, SHR, tapechunk10_7_p5
  // tapechunk10 tapechunk10_8: pin names not known; wires that end beside it: Write, Data, SHL, SHR, tapechunk10_8_p5
  // tapechunk10 tapechunk10_9: pin names not known; wires that end beside it: Write, Data, SHL, SHR, tapechunk10_9_p5
  // tapechunk10 tapechunk10_10: pin names not known; wires that end beside it: Write, Data, SHL, SHR, Lout, Rin, tapechunk10_10_p7
  assign or_1_out = tapechunk10_1_p7 | tapechunk10_2_p5;  // Or or_1, 4 bits wide
  assign or_2_out = or_1_out | tapechunk10_3_p5;  // Or or_2, 4 bits wide
  assign or_3_out = or_2_out | tapechunk10_4_p5;  // Or or_3, 4 bits wide
  assign or_4_out = or_3_out | tapechunk10_5_p5;  // Or or_4, 4 bits wide
  assign or_5_out = or_4_out | tapechunk10_6_p5;  // Or or_5, 4 bits wide
  assign or_6_out = or_5_out | tapechunk10_7_p5;  // Or or_6, 4 bits wide
  assign or_7_out = or_6_out | tapechunk10_8_p5;  // Or or_7, 4 bits wide
  assign or_8_out = or_7_out | tapechunk10_9_p5;  // Or or_8, 4 bits wide
  assign Value = or_8_out | tapechunk10_10_p7;  // Or or_9, 4 bits wide
endmodule
