// Digital circuit tapechunk1000.dig as structural Verilog
module tapechunk1000 (
  input  Lin,
  input  Write,
  input  [3:0] Data,
  input  SHL,
  input  SHR,
  input  Rin,
  output Rout,
  output [3:0] Value,
  output Lout
);

  wire tapechunk100_1_lout, tapechunk100_2_lout, tapechunk100_2_rout, tapechunk100_3_lout,
       tapechunk100_3_rout, tapechunk100_4_lout, tapechunk100_4_rout, tapechunk100_5_lout,
       tapechunk100_5_rout, tapechunk100_6_lout, tapechunk100_6_rout, tapechunk100_7_lout,
       tapechunk100_7_rout, tapechunk100_8_lout, tapechunk100_8_rout, tapechunk100_9_lout,
       tapechunk100_9_rout, tapechunk100_10_rout;
  wire [3:0] or_1_out, or_2_out, or_3_out, or_4_out, or_5_out, or_6_out, or_7_out, or_8_out,
       tapechunk100_1_value, tapechunk100_2_value, tapechunk100_3_value, tapechunk100_4_value,
       tapechunk100_5_value, tapechunk100_6_value, tapechunk100_7_value, tapechunk100_8_value,
       tapechunk100_9_value, tapechunk100_10_value;

  tapechunk100 tapechunk100_1 (
    .Lin(Lin), .Rout(Rout), .Write(Write), .Data(Data), .SHL(SHL), .SHR(SHR), .Value(tapechunk100_1_value),
    .Lout(tapechunk100_1_lout), .Rin(tapechunk100_2_rout));
  tapechunk100 tapechunk100_2 (
    .Lin(tapechunk100_1_lout), .Rout(tapechunk100_2_rout), .Write(Write), .Data(Data), .SHL(SHL), .SHR(SHR),
    .Value(tapechunk100_2_value), .Lout(tapechunk100_2_lout), .Rin(tapechunk100_3_rout));
  tapechunk100 tapechunk100_3 (
    .Lin(tapechunk100_2_lout), .Rout(tapechunk100_3_rout), .Write(Write), .Data(Data), .SHL(SHL), .SHR(SHR),
    .Value(tapechunk100_3_value), .Lout(tapechunk100_3_lout), .Rin(tapechunk100_4_rout));
  tapechunk100 tapechunk100_4 (
    .Lin(tapechunk100_3_lout), .Rout(tapechunk100_4_rout), .Write(Write), .Data(Data), .SHL(SHL), .SHR(SHR),
    .Value(tapechunk100_4_value), .Lout(tapechunk100_4_lout), .Rin(tapechunk100_5_rout));
  tapechunk100 tapechunk100_5 (
    .Lin(tapechunk100_4_lout), .Rout(tapechunk100_5_rout), .Write(Write), .Data(Data), .SHL(SHL), .SHR(SHR),
    .Value(tapechunk100_5_value), .Lout(tapechunk100_5_lout), .Rin(tapechunk100_6_rout));
  tapechunk100 tapechunk100_6 (
    .Lin(tapechunk100_5_lout), .Rout(tapechunk100_6_rout), .Write(Write), .Data(Data), .SHL(SHL), .SHR(SHR),
    .Value(tapechunk100_6_value), .Lout(tapechunk100_6_lout), .Rin(tapechunk100_7_rout));
  tapechunk100 tapechunk100_7 (
    .Lin(tapechunk100_6_lout), .Rout(tapechunk100_7_rout), .Write(Write), .Data(Data), .SHL(SHL), .SHR(SHR),
    .Value(tapechunk100_7_value), .Lout(tapechunk100_7_lout), .Rin(tapechunk100_8_rout));
  tapechunk100 tapechunk100_8 (
    .Lin(tapechunk100_7_lout), .Rout(tapechunk100_8_rout), .Write(Write), .Data(Data), .SHL(SHL), .SHR(SHR),
    .Value(tapechunk100_8_value), .Lout(tapechunk100_8_lout), .Rin(tapechunk100_9_rout));
  tapechunk100 tapechunk100_9 (
    .Lin(tapechunk100_8_lout), .Rout(tapechunk100_9_rout), .Write(Write), .Data(Data), .SHL(SHL), .SHR(SHR),
    .Value(tapechunk100_9_value), .Lout(tapechunk100_9_lout), .Rin(tapechunk100_10_rout));
  tapechunk100 tapechunk100_10 (
    .Lin(tapechunk100_9_lout), .Rout(tapechunk100_10_rout), .Write(Write), .Data(Data), .SHL(SHL), .SHR(SHR),
    .Value(tapechunk100_10_value), .Lout(Lout), .Rin(Rin));
  assign or_1_out = tapechunk100_1_value | tapechunk100_2_value;  // Or or_1, 4 bits wide
  assign or_2_out = or_1_out | tapechunk100_3_value;  // Or or_2, 4 bits wide
  assign or_3_out = or_2_out | tapechunk100_4_value;  // Or or_3, 4 bits wide
  assign or_4_out = or_3_out | tapechunk100_5_value;  // Or or_4, 4 bits wide
  assign or_5_out = or_4_out | tapechunk100_6_value;  // Or or_5, 4 bits wide
  assign or_6_out = or_5_out | tapechunk100_7_value;  // Or or_6, 4 bits wide
  assign or_7_out = or_6_out | tapechunk100_8_value;  // Or or_7, 4 bits wide
  assign or_8_out = or_7_out | tapechunk100_9_value;  // Or or_8, 4 bits wide
  assign Value = or_8_out | tapechunk100_10_value;  // Or or_9, 4 bits wide
endmodule
