// Digital circuit tapechunk10000.dig as structural Verilog
module tapechunk10000 (
  input  Lin,
  input  Write,
  input  [3:0] Data,
  input  SHL,
  input  SHR,
  input  Rin,
  output Rout,
  output [3:0] Value,
  output Lout
);

  wire tapechunk1000_1_lout, tapechunk1000_2_lout, tapechunk1000_2_rout, tapechunk1000_3_lout,
       tapechunk1000_3_rout, tapechunk1000_4_lout, tapechunk1000_4_rout, tapechunk1000_5_lout,
       tapechunk1000_5_rout, tapechunk1000_6_lout, tapechunk1000_6_rout, tapechunk1000_7_lout,
       tapechunk1000_7_rout, tapechunk1000_8_lout, tapechunk1000_8_rout, tapechunk1000_9_lout,
       tapechunk1000_9_rout, tapechunk1000_10_rout;
  wire [3:0] or_1_out, or_2_out, or_3_out, or_4_out, or_5_out, or_6_out, or_7_out, or_8_out,
       tapechunk1000_1_value, tapechunk1000_2_value, tapechunk1000_3_value, tapechunk1000_4_value,
       tapechunk1000_5_value, tapechunk1000_6_value, tapechunk1000_7_value, tapechunk1000_8_value,
       tapechunk1000_9_value, tapechunk1000_10_value;

  tapechunk1000 tapechunk1000_1 (
    .Lin(Lin), .Rout(Rout), .Write(Write), .Data(Data), .SHL(SHL), .SHR(SHR), .Value(tapechunk1000_1_value),
    .Lout(tapechunk1000_1_lout), .Rin(tapechunk1000_2_rout));
  tapechunk1000 tapechunk1000_2 (
    .Lin(tapechunk1000_1_lout), .Rout(tapechunk1000_2_rout), .Write(Write), .Data(Data), .SHL(SHL),
    .SHR(SHR), .Value(tapechunk1000_2_value), .Lout(tapechunk1000_2_lout), .Rin(tapechunk1000_3_rout));
  tapechunk1000 tapechunk1000_3 (
    .Lin(tapechunk1000_2_lout), .Rout(tapechunk1000_3_rout), .Write(Write), .Data(Data), .SHL(SHL),
    .SHR(SHR), .Value(tapechunk1000_3_value), .Lout(tapechunk1000_3_lout), .Rin(tapechunk1000_4_rout));
  tapechunk1000 tapechunk1000_4 (
    .Lin(tapechunk1000_3_lout), .Rout(tapechunk1000_4_rout), .Write(Write), .Data(Data), .SHL(SHL),
    .SHR(SHR), .Value(tapechunk1000_4_value), .Lout(tapechunk1000_4_lout), .Rin(tapechunk1000_5_rout));
  tapechunk1000 tapechunk1000_5 (
    .Lin(tapechunk1000_4_lout), .Rout(tapechunk1000_5_rout), .Write(Write), .Data(Data), .SHL(SHL),
    .SHR(SHR), .Value(tapechunk1000_5_value), .Lout(tapechunk1000_5_lout), .Rin(tapechunk1000_6_rout));
  tapechunk1000 tapechunk1000_6 (
    .Lin(tapechunk1000_5_lout), .Rout(tapechunk1000_6_rout), .Write(Write), .Data(Data), .SHL(SHL),
    .SHR(SHR), .Value(tapechunk1000_6_value), .Lout(tapechunk1000_6_lout), .Rin(tapechunk1000_7_rout));
  tapechunk1000 tapechunk1000_7 (
    .Lin(tapechunk1000_6_lout), .Rout(tapechunk1000_7_rout), .Write(Write), .Data(Data), .SHL(SHL),
    .SHR(SHR), .Value(tapechunk1000_7_value), .Lout(tapechunk1000_7_lout), .Rin(tapechunk1000_8_rout));
  tapechunk1000 tapechunk1000_8 (
    .Lin(tapechunk1000_7_lout), .Rout(tapechunk1000_8_rout), .Write(Write), .Data(Data), .SHL(SHL),
    .SHR(SHR), .Value(tapechunk1000_8_value), .Lout(tapechunk1000_8_lout), .Rin(tapechunk1000_9_rout));
  tapechunk1000 tapechunk1000_9 (
    .Lin(tapechunk1000_8_lout), .Rout(tapechunk1000_9_rout), .Write(Write), .Data(Data), .SHL(SHL),
    .SHR(SHR), .Value(tapechunk1000_9_value), .Lout(tapechunk1000_9_lout), .Rin(tapechunk1000_10_rout));
  tapechunk1000 tapechunk1000_10 (
    .Lin(tapechunk1000_9_lout), .Rout(tapechunk1000_10_rout), .Write(Write), .Data(Data), .SHL(SHL),
    .SHR(SHR), .Value(tapechunk1000_10_value), .Lout(Lout), .Rin(Rin));
  assign or_1_out = tapechunk1000_1_value | tapechunk1000_2_value;  // Or or_1, 4 bits wide
  assign or_2_out = or_1_out | tapechunk1000_3_value;  // Or or_2, 4 bits wide
  assign or_3_out = or_2_out | tapechunk1000_4_value;  // Or or_3, 4 bits wide
  assign or_4_out = or_3_out | tapechunk1000_5_value;  // Or or_4, 4 bits wide
  assign or_5_out = or_4_out | tapechunk1000_6_value;  // Or or_5, 4 bits wide
  assign or_6_out = or_5_out | tapechunk1000_7_value;  // Or or_6, 4 bits wide
  assign or_7_out = or_6_out | tapechunk1000_8_value;  // Or or_7, 4 bits wide
  assign or_8_out = or_7_out | tapechunk1000_9_value;  // Or or_8, 4 bits wide
  assign Value = or_8_out | tapechunk1000_10_value;  // Or or_9, 4 bits wide
endmodule
