// Digital circuit tapeseg.dig as structural Verilog
module tapeseg (
  input  Write,
  input  SHR,
  input  SHL,
  input  [3:0] Data,
  input  Lin,
  input  Rin,
  output [3:0] Value,
  output Rout,
  output Lout
);

  wire and_1_out, and_2_out, and_3_out, or_1_out, or_2_out, R_W_value;
  wire [3:0] Symbol_value;

  or or_1 (or_1_out, SHL, SHR);
  and and_1 (and_1_out, Lin, SHR);
  and and_2 (and_2_out, SHL, Rin);
  or or_2 (or_2_out, and_1_out, and_2_out);
  flipflop R_W (.Data(or_2_out), .Write(or_1_out), .Value(R_W_value));
  and and_3 (and_3_out, Write, R_W_value);
  tapecell Symbol (.Data(Data), .Write(and_3_out), .Value(Symbol_value));
  assign Value = R_W_value ? Symbol_value : 4'bz;  // Driver driver_1
  flipflop Shift (.Data(R_W_value), .Write(Write), .Value(Lout));

  assign Rout = Lout;
endmodule
