// Digital circuit testing.dig as structural Verilog
module testing (
  input  clk
);

  wire g0, start_1_acto, start_1_fqo, t, t2, t3, testing_shl, testing_shr, undriven, undriven_2, undriven_3,
       undriven_4;

  start start_1 (.fqi(t), .Acti(clk), .fqo(start_1_fqo), .Acto(start_1_acto));
  state #(.generic("// shift := 0b0011 << 4 + 0b0000 << 4 + 0b0000 << 4 + 0b0000; //")) testing (
    .Lookup(16'h2000), .from_q(start_1_fqo), .Activating(start_1_acto), .Q(t2), ._1_Q(t2), ._0_Q(t2),
    ._1_Q_2(t2), ._0_Q_2(t2), .H_Q(t2), .H1_Q(t2), .H0_Q(t2), .Q_2(t2), ._0_Q_3(t2), ._1_Q_3(t2), ._00_Q(t2),
    ._01_Q(t2), ._10_Q(t2), ._11_Q(t2), .Q_3(t2), .SHL(testing_shl), .SHR(testing_shr), .\Γ (g0),
    .\_1_Γ (g0), .\_0_Γ (g0), .\_1_Γ_2 (g0), .\_0_Γ_2 (g0), .\H_Γ (g0), .\H1_Γ (g0), .\H0_Γ (g0), .\Γ_2 (g0),
    .\_0_Γ_3 (g0), .\_1_Γ_3 (g0), .\_00_Γ (g0), .\_01_Γ (g0), .\_10_Γ (g0), .\_11_Γ (g0), .\Γ_3 (g0));
  // state #(.generic("shift := 0x3000;")) testing2: pin names not known; wires that end beside it: t2, clk, 16'h400, t3
  // state #(.generic("shift := 0x3000;")) testing3: pin names not known; wires that end beside it: t3, clk, 16'h10, t
  LED led_1 (.in(testing_shl));
  LED led_2 (.in(testing_shr));
  LED led_3 (.in(undriven));
  LED led_4 (.in(undriven_2));
  LED led_5 (.in(undriven_3));
  LED led_6 (.in(undriven_4));
endmodule
